// Logisim project 1bit_CPU.circ as structural Verilog: 2 circuits, main circuit One_Bit_CPU
module CPU_and_ProgramRom (
);

  wire MasterClock_out, por_1_out;
  wire [7:0] ProgramROM_data;
  wire [10:0] one_bit_cpu_1_dataaddress;
  wire [11:0] one_bit_cpu_1_instructionaddress;

  Clock MasterClock (.out(MasterClock_out));
  POR por_1 (.out(por_1_out));
  ROM #(.addrWidth(12)) ProgramROM (.addr(one_bit_cpu_1_instructionaddress), .data(ProgramROM_data));
  One_Bit_CPU one_bit_cpu_1 (
    .Clock(MasterClock_out), .Reset(por_1_out), .DataIn(one_bit_cpu_1_dataaddress[0]),
    .InstructionIn(ProgramROM_data), .DataAddress(one_bit_cpu_1_dataaddress),
    .InstructionAddress(one_bit_cpu_1_instructionaddress));  // open: DataOut, Write

  // Notes on the sheet:
  //   contents of ProgramROM (hex, n*v repeats v):
  //   c8 0 c8 3 c8 1 c8 2 cc 0 c8 1 88 a0 8c a0 60 62 40 a0 41 a0 42 a0 43 a0 88 60 8c 61 0 a0 8c 1 a0 88
  //   1 a0 88 0 a0 8c 60 88 20 61 1 80 1 40 88 41 f0 37 80 62 e0 3b 80 63 80 e0 40 80 64 e0 44 80 65 8c c8
  //   2 80 c8 3 c0 0 c0 1
endmodule

module One_Bit_CPU (
  input  Clock,
  input  Reset,
  input  DataIn,
  input  [7:0] InstructionIn,
  output DataOut,
  output Write,
  output [10:0] DataAddress,
  output [11:0] InstructionAddress
);

  wire Accumulator_q, and_1_out, Clk0, Clk1, Clk2, EitherJMP_out, FetchNext_qn, JMPT_out, multiplexer_1_out,
       not_1_out, not_2_out, not_3_out, or_1_out, Registers_dout;
  wire [1:0] ClockDivider_q;
  wire [2:0] StackPointer_q;
  wire [6:0] FetchNext_q;
  wire [11:0] multiplexer_2_out, ProgramStack_dout;
  wire [11:8] InstructionRegister_q;
  wire [19:0] Microcode_data;

  Counter #(.max('h2), .width(2)) ClockDivider (
    .load(1'b0), .count(1'b1), .Q(ClockDivider_q), .up(1'b1), .clk(Clock), .clr(Reset));  // open: D, carry
  Demultiplexer #(.enable("true"), .select(2)) demultiplexer_1 (
    .out0(Clk0), .out1(Clk1), .out2(Clk2), .in(1'b1), .sel(ClockDivider_q), .en(not_1_out));  // open: out3
  not not_1 (not_1_out, Reset);
  ROM #(.addrWidth(7), .dataWidth(20)) Microcode (
    .addr({FetchNext_q[6:3], InstructionRegister_q[11:10], FetchNext_q[0]}), .data(Microcode_data));
  Counter #(.max('h7), .width(3)) StackPointer (
    .clr(Reset), .load(Microcode_data[18]), .up(Microcode_data[19]), .count(1'b1), .clk(Clk0),
    .Q(StackPointer_q));  // open: D, carry
  // Probe on ClockDivider_q
  // Probe on Microcode_data
  and and_1 (and_1_out, Registers_dout, Accumulator_q);
  or or_1 (or_1_out, Registers_dout, Accumulator_q);
  not not_2 (not_2_out, Accumulator_q);
  RAM #(.addrWidth(3), .dataWidth(12)) ProgramStack (
    .addr(StackPointer_q), .we(Microcode_data[16]), .oe(Microcode_data[17]), .clk(Clk0),
    .din(InstructionAddress), .dout(ProgramStack_dout));
  Multiplexer #(.select(3)) multiplexer_1 (
    .in0(1'b0), .in1(1'b1), .in2(Registers_dout), .in3(and_1_out), .in4(or_1_out), .in5(not_2_out),
    .in6(DataIn), .out(multiplexer_1_out), .sel(Microcode_data[2:0]));  // open: in7
  T_Flip_Flop FetchNext (
    .T(Microcode_data[15]), .clk(Clk1), .Q(FetchNext_q[0]), .Qn(FetchNext_qn), .reset(Reset));  // open: preset
  Register #(.width(1)) Accumulator (
    .D(multiplexer_1_out), .en(Microcode_data[3]), .clk(Clk2), .Q(Accumulator_q), .clr(Reset));
  Register InstructionRegister (
    .D(InstructionIn), .en(FetchNext_qn), .clk(Clk0), .Q({FetchNext_q[6:3], InstructionRegister_q}),
    .clr(Reset));
  RAM #(.addrWidth(5), .dataWidth(1)) Registers (
    .addr({FetchNext_q[3], InstructionRegister_q}), .we(Microcode_data[4]), .oe(Microcode_data[5]),
    .clk(Clk1), .din(Accumulator_q), .dout(Registers_dout));
  or EitherJMP (EitherJMP_out, Microcode_data[12], JMPT_out);
  Multiplexer #(.width(12)) multiplexer_2 (
    .in0({InstructionRegister_q, InstructionIn}), .in1(ProgramStack_dout), .out(multiplexer_2_out),
    .sel(Microcode_data[14]));
  and JMPT (JMPT_out, Microcode_data[11], Accumulator_q);
  Counter #(.max('hfff), .width(12)) ProgramCounter (
    .clr(Reset), .load(EitherJMP_out), .up(not_3_out), .count(1'b1), .clk(Clk0), .D(multiplexer_2_out),
    .Q(InstructionAddress));  // open: carry
  not not_3 (not_3_out, Microcode_data[13]);
  Counter #(.max('h7ff), .width(11)) DataAddressLatch (
    .clr(Reset), .load(Microcode_data[8]), .up(Microcode_data[9]), .count(Microcode_data[10]), .clk(Clk1),
    .D({InstructionRegister_q[10:8], InstructionIn}), .Q(DataAddress));  // open: carry
  and and_2 (DataOut, Accumulator_q, Microcode_data[6]);
  and and_3 (Write, Microcode_data[7], Clk2);

  // Other names for the same wires on the sheet: Rst = Reset

  // Notes on the sheet:
  //   contents of Microcode (hex, n*v repeats v):
  //   2b 3 2b 3 2b 3 2b 3 2b 3 2b 3 2b 3 2b 3 2c 4 2c 4 2c 4 2c 4 2c 4 2c 4 2c 4 2c 4 2a 0 2a 0 2a 0 2a 0
  //   2a 0 2a 0 2a 0 2a 0 10 0 10 0 10 0 10 0 10 0 10 0 10 0 10 0 2d 0 0 0 8 0 9 9*0 c0 7*0 e 7*0 8500
  //   800e 8500 800e 8500 80c0 8500 80c0 8*0 8000 8800 8000 8800 8000 8800 8000 8800 8000 9000 8000 9000
  //   8000 9000 8000 9000
endmodule
